# Fritzing sketch AirQ (saved by Fritzing 0.9.4)
circuit board: 4.67811cm x 3.37928cm

parts:
  Q1 = NPN-Transistor [package="TO92 [THT]"]
  Q2 = NPN-Transistor [package="TO92 [THT]"]
  Q3 = NPN-Transistor [package="TO92 [THT]"]
  Q4 = NPN-Transistor [package="TO92 [THT]"]
  C1 = Electrolytic Capacitor [capacitance=1µF package="100 mil [THT, electrolytic]"]
  Arduino_ProMini = Arduino Pro Mini (5V)
  YELLOW = Super Flux LED blue [color=Yellow]
  GREEN = Super Flux LED blue [color=Green]
  RED = Super Flux LED blue [color=Red]
  J1 = Piezo Speaker
  R1 = Resistor [tolerance=±5% resistance=220 package="2010 [SMD]"]
  R2 = Resistor [tolerance=±5% resistance=220 package="2010 [SMD]"]
  R3 = Resistor [tolerance=±5% resistance=220 package="2010 [SMD]"]
  U1 = Mini-USB _B_ connector with 5th pin broken out. [package=usb-minib]
  LCD1 = LCD screen
  J2 = female pin header, 5 pins [form="♀ (female)"]

nets:
  GND: Q1.E, Q2.E, Q3.E, Q4.E, C1.-, Arduino_ProMini.GND, U1.MTN2, U1.MTN3, U1.MTN1, U1.MTN4, U1.GND, LCD1.VSS, J2.pin2, J2.pin5
  N1: Q1.B, Arduino_ProMini.D10
  N2: Q1.C, RED.cathode
  N3: Q2.B, Arduino_ProMini.MOSI
  N4: Q2.C, YELLOW.cathode
  N5: Q3.B, Arduino_ProMini.MISO
  N6: Q4.B, Arduino_ProMini.SCK
  N7: Q4.C, J1.pin1
  N8: C1.+, Arduino_ProMini.VCC, J1.pin2
  N9: Arduino_ProMini.A4, J2.pin4
  N10: Arduino_ProMini.A5, J2.pin3
  N11: Arduino_ProMini.RAW, R1.Pin_1, R2.Pin_1, R3.Pin_1, U1.VBUS
  N12: Arduino_ProMini.D8, LCD1.LED+
  N13: Arduino_ProMini.D7, LCD1.DB7
  N14: Arduino_ProMini.D6, LCD1.DB6
  N15: Arduino_ProMini.D5, LCD1.DB5
  N16: Arduino_ProMini.D4, LCD1.DB4
  N17: Arduino_ProMini.D3, LCD1.E
  N18: Arduino_ProMini.D2, LCD1.RS
  N19: YELLOW.anode, R2.Pin_0
  N20: GREEN.anode, R1.Pin_0
  N21: RED.anode, R3.Pin_0
